# Fritzing sketch Laser_Gate_Schematic (saved by Fritzing 0.9.2b)
circuit board: 8.49041cm x 6.1847cm
breadboards: 1

parts:
  Part1 = Breadboard Power Supply Board SMD
  IC1 = IC, DIP package, 8 pins [chip_label=IC]
  C1 = Ceramic Capacitor [capacitance=100nF package="100 mil [THT, multilayer]"]
  +5V = female pin header, 1 pin [form="♀ (female)"]
  C2 = Ceramic Capacitor [capacitance=100nF package="100 mil [THT, multilayer]"]
  R1 = Resistor [tolerance=±5% resistance=1k package=THT]
  C3 = Ceramic Capacitor [capacitance=100nF package="100 mil [THT, multilayer]"]
  Input = BNC [package=bnc]
  R2 = Resistor [tolerance=±5% resistance=1k package=THT]
  IC2 = IC, DIP package, 8 pins [chip_label=IC]
  C4 = Ceramic Capacitor [capacitance=100nF package="100 mil [THT, multilayer]"]
  R3 = Rotary Potentiometer (Small) [maximum_resistance=100kΩ package=THT]
  R4 = Resistor [tolerance=±5% resistance=1k package=THT]
  R5 = Resistor [tolerance=±5% resistance=220 package=THT]
  R6 = Resistor [tolerance=±5% resistance=220 package=THT]
  R7 = Resistor [tolerance=±5% resistance=220 package=THT]
  R8 = Resistor [tolerance=±5% resistance=220 package=THT]
  R9 = Resistor [tolerance=±5% resistance=220 package=THT]
  IC3 = IC, DIP package, 8 pins [chip_label=IC]
  J4 = female pin header, 1 pin [form="♀ (female)"]
  C5 = Ceramic Capacitor [capacitance=100nF package="100 mil [THT, multilayer]"]
  R10 = Resistor [tolerance=±5% resistance=220 package=THT]
  J5 = female pin header, 1 pin [form="♀ (female)"]
  R11 = Rotary Potentiometer (Small) [maximum_resistance=100kΩ package=THT]
  R12 = Resistor [tolerance=±5% resistance=220 package=THT]
  IC4 = IC, DIP package, 14 pins [chip_label=IC]
  Output = BNC [package=bnc]
  C8 = Ceramic Capacitor [capacitance=100nF package="100 mil [THT, multilayer]"]
  C9 = Ceramic Capacitor [capacitance=100nF package="100 mil [THT, multilayer]"]
  C10 = Ceramic Capacitor [capacitance=100nF package="100 mil [THT, multilayer]"]
  C11 = Ceramic Capacitor [capacitance=100nF package="100 mil [THT, multilayer]"]
  J1 = female pin header, 1 pin [form="♀ (female)"]
  GND = female pin header, 1 pin [form="♀ (female)"]
  J3 = female pin header, 1 pin [form="♀ (female)"]

nets:
  GND: Part1.GND, IC1.pin4, C1.1, C2.0, Input.GND, IC2.pin4, C4.1, R3.leg1, IC3.pin4, C5.1, R11.leg1, IC4.pin4, IC4.pin5, IC4.pin7, Output.GND, C8.0, C9.0, C10.0, C11.0, J1.pin1, GND.pin1
  N1: Part1.VCC, IC1.pin7, C1.0, +5V.pin1, IC2.pin7, R3.leg2, IC3.pin7, R11.leg2, IC4.pin14
  N2: IC1.pin2, R1.Pin_0, C3.0
  N3: IC1.pin3, R2.Pin_1
  N4: IC1.pin6, C2.1, R1.Pin_1, C3.1, R6.Pin_0, R7.Pin_0, R8.Pin_0, R9.Pin_0
  N5: Input.OUT, R2.Pin_0
  N6: IC2.pin2, R5.Pin_0
  N7: IC2.pin3, R4.Pin_1
  N8: IC2.pin6, C4.0, IC4.pin1, IC4.pin2, Output.OUT, J3.pin1
  N9: R3.wiper, R4.Pin_0
  N10: R5.Pin_1, R6.Pin_1, R7.Pin_1, R8.Pin_1, R9.Pin_1, R10.Pin_0, J5.pin1, C8.1, C9.1, C10.1, C11.1
  N11: IC3.pin2, R12.Pin_0
  N12: IC3.pin3, R10.Pin_1
  N13: IC3.pin6, J4.pin1, C5.0, IC4.pin3
  N14: R11.wiper, R12.Pin_1

notes:
  Output
  Input
  A
  B
